# Fritzing sketch Prosthetic Hand (saved by Fritzing 0.9.3b)
breadboards: 1

parts:
  Part1 = Arduino Nano (Rev3.0)
  J1 = Basic Servo
  M1 = Dagu DGServo 9g (Top view) [part_number=RS001B]
  M2 = Dagu DGServo 9g (Top view) [part_number=RS001B]
  R2 = Resistor [tolerance=±5% resistance=220 package="0805 [SMD]"]
  R1 = Basic Force Sensing Resistor (FSR) [package=THT]

nets:
  GND: Part1.GND, J1.gnd, M1.gnd, M2.gnd, R2.Pin_0
  N1: Part1.D2, M1.pulse
  N2: Part1.D4, J1.pulse
  N3: Part1.D6, M2.pulse
  VCC: Part1.5V, J1.vcc, M1.vcc, M2.vcc, R1.pin_1
  N4: Part1.A0, R2.Pin_1, R1.pin_0
